# Fritzing sketch schematics_VNH2SP30 (saved by Fritzing 0.9.6b)
breadboards: 1

parts:
  U1 = atmega328 [package=dip]
  R1 = Resistor [tolerance=±5% power=0.25 resistance=4.7k package=THT]
  R2 = Resistor [tolerance=±5% power=0.25 resistance=4.7k package=THT]
  R3 = Resistor [tolerance=±5% power=0.25 resistance=4.7k package=THT]
  LED1 = LED - 5mm [color="Red (633nm)" current=0.030 package="5 mm [THT]"]
  LED2 = LED - 5mm [color="Red (633nm)" current=0.030 package="5 mm [THT]"]
  LED3 = LED - 5mm [color="Red (633nm)" current=0.030 package="5 mm [THT]"]
  M1 = DC Motor
  Open = Round Pushbutton
  Fully_open = SWITCH-SPST-2 [package=switch-spst-vertical]
  Close = Round Pushbutton
  Emergency = Round Pushbutton
  Fully_closed = SWITCH-SPST-2 [package=switch-spst-vertical]
  Solenoid = Solenoid
  MOSFET = Basic FET N-Channel [package="TO220 [THT]"]
  D1 = Rectifier Diode [part_number=1N4001 package="300 mil [THT]"]
  R5 = Resistor [tolerance=±5% power=0.25 resistance=1k package=THT]
  R4 = Resistor [tolerance=±5% power=0.25 resistance=4.7k package=THT]
  LED4 = LED - 5mm [color="Red (633nm)" current=0.030 package="5 mm [THT]"]
  U3 = RF-LINK_TX [package=rf-link_tx]  # not connected
  U4 = RF-LINK_RX [package=rf-link_rx]
  ANT1 = Antenna
  U5 = VNH2SP30 [package=vnh2sp30]

nets:
  N1: U1.RESET/PC6, R4.Pin_1
  N2: U1.D0_(RX)/PD0, U4.DATA
  N3: U1.D8, Open.leg1
  N4: U1.D9_(PWM), Close.leg1
  N5: U1.D10_(PWM), Fully_open.O
  N6: U1.D11_(PWM), Fully_closed.O
  N7: U1.D12, Emergency.leg1
  N8: U1.A0, R1.Pin_0
  N9: U1.A1, R2.Pin_0
  N10: U1.A2, R3.Pin_0
  N11: U1.A3, U5.INB
  N12: U1.A4, U5.INA
  N13: U1.A5, R5.Pin_1
  N14: R1.Pin_1, LED1.anode
  N15: R2.Pin_1, LED2.anode
  N16: R3.Pin_1, LED3.anode
  GND: LED1.cathode, LED2.cathode, LED3.cathode, Open.leg0, Fully_open.P, Close.leg0, Emergency.leg0, Fully_closed.P, MOSFET.source, LED4.cathode, U4.GND, U5.GNDB, U5.GNDA
  N17: M1.pin_1, U5.OUTA
  N18: M1.pin_2, U5.OUTB
  12V: Solenoid.pin1, D1.anode, U5.VCC
  N19: Solenoid.pin2, MOSFET.drain, D1.cathode
  N20: MOSFET.gate, R5.Pin_0
  N21: R4.Pin_0, LED4.anode
  5V: U4.+5V, U5.EN_DIAA, U5.PWM, U5.EN_DIAB
  N22: U4.ANT, ANT1.antenna_lead

notes:
  R1, R2, R3, R4 = 330 Ohm
  R5 = 1k

custom parts:
  atmega328: Atmel ATmega328 microcontroller.
